# Fritzing sketch Basic-Circuit (saved by Fritzing 0.9.3b)
breadboards: 2

parts:
  Part1 = Arduino Mega 2560 (Rev3)
  S1 = Pushbutton [package="[THT]"]
  S2 = Pushbutton [package="[THT]"]
  S3 = Pushbutton [package="[THT]"]
  S4 = Pushbutton [package="[THT]"]
  S5 = Pushbutton [package="[THT]"]
  S6 = Pushbutton [package="[THT]"]
  S7 = Pushbutton [package="[THT]"]
  S8 = Pushbutton [package="[THT]"]
  S9 = Pushbutton [package="[THT]"]
  S10 = Pushbutton [package="[THT]"]
  S11 = Pushbutton [package="[THT]"]
  R1 = Rotary Potentiometer (Small) [maximum_resistance=100kΩ package=THT]
  S12 = Pushbutton [package="[THT]"]
  S13 = Pushbutton [package="[THT]"]
  S14 = Pushbutton [package="[THT]"]
  S15 = Pushbutton [package="[THT]"]
  S16 = Pushbutton [package="[THT]"]

nets:
  N1: Part1.A0, R1.wiper
  N2: Part1.GND, S1.Pin_3, S1.Pin_4, S2.Pin_3, S2.Pin_4, S3.Pin_3, S3.Pin_4, S4.Pin_3, S4.Pin_4, S5.Pin_3, S5.Pin_4, S6.Pin_3, S6.Pin_4, S7.Pin_3, S7.Pin_4, S8.Pin_3, S8.Pin_4, S9.Pin_3, S9.Pin_4, S10.Pin_3, S10.Pin_4, S11.Pin_3, S11.Pin_4, R1.leg1, S12.Pin_3, S12.Pin_4, S13.Pin_3, S13.Pin_4, S14.Pin_3, S14.Pin_4, S15.Pin_3, S15.Pin_4, S16.Pin_3, S16.Pin_4
  N3: Part1.D12_PWM, S13.Pin_1, S13.Pin_2
  N4: Part1.D11_PWM, S15.Pin_1, S15.Pin_2
  N5: Part1.D10_PWM, S14.Pin_1, S14.Pin_2
  N6: Part1.D9_PWM, S16.Pin_1, S16.Pin_2
  N7: Part1.D8_PWM, S12.Pin_1, S12.Pin_2
  N8: Part1.5V, R1.leg2
  N9: Part1.D22, S1.Pin_1, S1.Pin_2
  N10: Part1.D24, S2.Pin_1, S2.Pin_2
  N11: Part1.D26, S4.Pin_1, S4.Pin_2
  N12: Part1.D28, S3.Pin_1, S3.Pin_2
  N13: Part1.D30, S6.Pin_1, S6.Pin_2
  N14: Part1.D32, S5.Pin_1, S5.Pin_2
  N15: Part1.D34, S7.Pin_1, S7.Pin_2
  N16: Part1.D36, S9.Pin_1, S9.Pin_2
  N17: Part1.D38, S8.Pin_1, S8.Pin_2
  N18: Part1.D40, S10.Pin_1, S10.Pin_2
  N19: Part1.D52, S11.Pin_1, S11.Pin_2
